# Fritzing sketch Esquema (saved by Fritzing 0.9.10b)

parts:
  Componente1 = RFID-RC522-v3
  Componente2 = 4x4 Keypad [part_number=101207]
  Componente3 = Arduino Uno (Rev3)
  Componente4 = Jtron 1 Channel Optoisolated Relay Module [package=relay]
  M1 = gear-motor

nets:
  N1: Componente1.SDA, Componente3.D10_PWM/SS
  N2: Componente1.SCK, Componente3.D13/SCK
  N3: Componente1.MOSI, Componente3.D11_PWM/MOSI
  N4: Componente1.MISO, Componente3.D12/MISO
  GND: Componente1.GND, Componente3.GND, Componente4.GND
  N5: Componente1.RST, Componente3.D9_PWM
  3.3V: Componente1.3.3V, Componente3.3V3
  N6: Componente2.1, Componente3.A0
  N7: Componente2.2, Componente3.A1
  N8: Componente2.3, Componente3.A2
  N9: Componente2.4, Componente3.A3
  N10: Componente2.5, Componente3.D2
  N11: Componente2.6, Componente3.D1/TX
  N12: Componente2.7, Componente3.D0/RX
  N13: Componente3.D3_PWM, Componente4.IN1
  5V: Componente3.5V, Componente4.VCC
  N14: Componente4.NC, M1.pin_2

custom parts:
  RFID-RC522-v3: A simple China made RFID-RC522 Reader (6x4 cm); do check the pin labels, as this is a MFRC522 based clone.
  4x4 Keypad: Matrix membrane keypad 4x4
